# Fritzing sketch gg02 (saved by Fritzing 0.9.3b)
circuit board: 3.72cm x 5cm
breadboards: 1

parts:
  S3 = SWITCH-MOMENTARY-2 [package=tactile-switch-1101ne]
  S4 = SWITCH-MOMENTARY-2 [package=tactile-switch-1101ne]
  S5 = SWITCH-MOMENTARY-2 [package=tactile-switch-1101ne]
  S6 = SWITCH-MOMENTARY-2 [package=tactile-switch-1101ne]
  o = SWITCH-MOMENTARY-2 [package=tactile-switch-1101ne]
  x = SWITCH-MOMENTARY-2 [package=tactile-switch-1101ne]
  X1 = USB Connectors [package=usb-microb]
  U3 = TQFP32 [chip_label=IC package=TQFP]
  U1 = AT25FS010 [package=so08wide]
  U2 = ST7735 TFT [part_number=ST7735 package=14pin]
  SWC = Pad [width=1.27 height=2.54 connect=center]
  SWD = Pad [width=1.27 height=2.54 connect=center]
  C1 = Ceramic Capacitor [capacitance=1µF package="0603 [SMD, multilayer]"]
  U4 = Voltage Regulator LDO [package=sot23-5]
  on_off = SPST Switch [package=switch-spst-smd-a]
  C2 = Ceramic Capacitor [capacitance=1µF package="0603 [SMD, multilayer]"]
  D1 = Rectifier Diode [package="Melf DO-213 AA [SMD]"]
  +_- = female pin header, 2 pins [form="♀ (female)"]
  - = female pin header, 1 pin [form="♀ (female)"]
  + = female pin header, 1 pin [form="♀ (female)"]
  U5 = MCP73831T-2ACIOT Lithium Charger IC [package=sot23-5]
  R1 = Resistor [tolerance=±5% resistance=10k package="0402 [SMD]"]
  R2 = Resistor [tolerance=±5% resistance=10k package="0402 [SMD]"]
  R3 = Resistor [tolerance=±5% resistance=2.2k package="0402 [SMD]"]
  chg = smd LED [color="Red (633nm)" package="0603 [SMD]"]
  X4 = Pad [width=6.4000000000000004 height=0.59999999999999998 connect=west]
  reset = Pad [width=6.4000000000000004 height=0.59999999999999998 connect=center]
  speaker2 = Pad [width=5.0800000000000001 height=1.27 connect=center]
  speaker = Pad [width=5.0800000000000001 height=1.27 connect=center]
  R4 = Resistor [tolerance=±5% resistance=10k package="0402 [SMD]"]

nets:
  GND: S3.1, S4.2, S5.2, S6.1, o.2, x.1, X1.GND, U3.GND, U1.GND, U2.GND, U2.LED-, U2.CS, C1.0, U4.GND, C2.0, +_-.pin2, -.pin1, U5.VSS, R2.Pin_1, reset.pad, speaker2.pad
  N1: S3.2, U3.PA03
  N2: S4.1, U3.PA04
  N3: S5.1, U3.PA05
  N4: S6.2, U3.PA23
  N5: o.1, U3.PA01
  N6: x.2, U3.PA00
  N7: X1.D+, U3.PA25
  N8: X1.D-, U3.PA24
  N9: X1.VBUS, U4.IN, U4.EN, D1.cathode, U5.VDD
  N10: U3.PA02, speaker.pad
  N11: U3.PA06, U2.MOSI
  N12: U3.PA07, U2.SCK
  VCC: U3.VDDANA, U3.VDDIN, U1.WP, U1.HOLD, U1.VCC, U2.VCC, U2.IOVCC, U4.OUT, C2.1, R1.Pin_1, R4.Pin_0
  N13: U3.PA08, U2.D/C
  N14: U3.PA11, U1.CS, R1.Pin_0
  N15: U3.PA16, U1.SI
  N16: U3.PA17, U1.SCK
  N17: U3.PA19, U1.SO
  N18: U3.!RESET, U2.!RESET, X4.pad
  N19: U3.VDDCORE, C1.1
  N20: U3.PA30, SWD.pad
  N21: U3.PA31, SWC.pad
  N22: U2.LED+, R4.Pin_1
  N23: on_off.O, on_off.P, +_-.pin1, +.pin1
  N24: on_off.S, D1.anode, U5.VBAT, chg.anode
  N25: U5.STAT, R3.Pin_1
  N26: U5.PROG, R2.Pin_0
  N27: R3.Pin_0, chg.cathode

notes:
  02

custom parts:
  ST7735 TFT: Connector for 14-pin ST7735 TFT display.
