# Fritzing sketch gg07 (saved by Fritzing 0.9.3b)
circuit board: 4.19999cm x 4.99999cm
breadboards: 1

parts:
  X1 = USB Connectors [package=usb-microb]
  U3 = TQFP32 [chip_label=IC package=TQFP]
  U1 = AT25FS010 [package=so08wide]
  U2 = ST7735 TFT [part_number=ST7735 package=14pin]
  C1 = Ceramic Capacitor [capacitance=1µF package="0603 [SMD, multilayer]"]
  U4 = Voltage Regulator LDO [package=sot23-5]
  C2 = Ceramic Capacitor [capacitance=1µF package="0603 [SMD, multilayer]"]
  D1 = Rectifier Diode [package="Melf DO-213 AA [SMD]"]
  U5 = MCP73831T-2ACIOT Lithium Charger IC [package=sot23-5]
  R1 = Resistor [tolerance=±5% resistance=10k package="0402 [SMD]"]
  R2 = Resistor [tolerance=±5% resistance=10k package="0402 [SMD]"]
  R3 = Resistor [tolerance=±5% resistance=2.4k package="0402 [SMD]"]
  CHARGE = smd LED [color="Orange (605nm)" package="0603 [SMD]"]
  R4 = Resistor [tolerance=±5% resistance=300 package="0402 [SMD]"]
  ON = SPST Switch [package=switch-spst-smd-a]
  Pad5 = Pad [width=7 height=2 connect=center]
  R6 = Resistor [tolerance=±5% resistance=47k package="0402 [SMD]"]
  U5_2 = PAM8391 [part_number=PAM8301AAF package=SOT23-6]
  R8 = Resistor [tolerance=±10% resistance=10k package="0402 [SMD]"]
  R7 = Resistor [tolerance=±10% resistance=47k package="0402 [SMD]"]
  C3 = Ceramic Capacitor [capacitance=1µF package="0603 [SMD, multilayer]"]
  SPKR = Pad [width=1.27 height=2.54 connect=center]
  + = Pad [width=1.27 height=2.54 connect=center]
  +_2 = Pad [width=2.6000000000000001 height=3 connect=center]
  SWCLK = Pad [width=2.54 height=2.54 connect=center]
  SWDIO = Pad [width=2.54 height=2.54 connect=center]
  - = Pad [width=2.6000000000000001 height=3 connect=center]
  R5 = Resistor [tolerance=±5% resistance=47k package="0402 [SMD]"]
  RESET = Pad [width=1.27 height=1.8999999999999999 connect=center]
  OFF = Pad [width=1.27 height=1.8999999999999999 connect=center]
  S6 = SKPMAPE010 [package=SKPMAPE010]
  S3 = SKPMAPE010 [package=SKPMAPE010]
  S4 = SKPMAPE010 [package=SKPMAPE010]
  o = SKPMAPE010 [package=SKPMAPE010]
  x = SKPMAPE010 [package=SKPMAPE010]
  S5 = SKPMAPE010 [package=SKPMAPE010]

nets:
  N1: X1.D+, U3.PA25
  N2: X1.D-, U3.PA24
  GND: X1.GND, U3.GND, U1.GND, U2.GND, U2.LED-, C1.0, U4.GND, C2.0, U5.VSS, R2.Pin_1, Pad5.pad, R6.Pin_0, U5_2.GND, -.pad, RESET.pad, S6.1, S3.1, S4.2, o.2, x.1, S5.1
  N3: X1.VBUS, U4.IN, U4.EN, D1.cathode, U5.VDD
  N4: U3.PA00, o.1
  N5: U3.PA01, x.2
  N6: U3.PA02, R7.Pin_1
  N7: U3.PA03, S3.2
  N8: U3.PA04, S6.2
  N9: U3.PA05, S5.2
  N10: U3.PA06, U2.MOSI
  N11: U3.PA07, U2.SCK
  3.3V: U3.VDDANA, U3.VDDIN, U1.WP, U1.HOLD, U1.VCC, U2.VCC, U2.IOVCC, U4.OUT, C2.1, R1.Pin_1, R4.Pin_0, U5_2.VDD, R8.Pin_1
  N12: U3.PA08, U2.CS
  N13: U3.PA09, U2.D/C
  N14: U3.PA11, R6.Pin_1, R5.Pin_0
  N15: U3.PA16, U1.SI
  N16: U3.PA17, U1.SCK
  N17: U3.PA18, U1.CS, R1.Pin_0
  N18: U3.PA19, U1.SO
  N19: U3.PA22, U5_2.!SD, R8.Pin_0
  N20: U3.PA23, S4.1
  N21: U3.!RESET, U2.!RESET, OFF.pad
  N22: U3.VDDCORE, C1.1
  N23: U3.PA30, SWCLK.pad
  N24: U3.PA31, SWDIO.pad
  N25: U2.LED+, R4.Pin_1
  N26: D1.anode, U5.VBAT, CHARGE.anode, ON.O, ON.P, R5.Pin_1
  N27: U5.STAT, R3.Pin_1
  N28: U5.PROG, R2.Pin_0
  N29: R3.Pin_0, CHARGE.cathode
  N30: ON.S, +_2.pad
  N31: U5_2.OUT+, +.pad
  N32: U5_2.IN, C3.1
  N33: U5_2.OUT-, SPKR.pad
  N34: R7.Pin_0, C3.0

notes:
  http://hackaday.io/project/27629

custom parts:
  ST7735 TFT: Connector for 14-pin ST7735 TFT display.
  SKPMAPE010: Various NO switches- pushbuttons, reed, etc
