# Fritzing sketch ngame02 (saved by Fritzing 0.9.3b)
circuit board: 2.64966cm x 2.65cm
breadboards: 1

parts:
  gnd = Pad [width=0.40000000000000002 height=5.0800000000000001 connect=south]
  led+ = Pad [width=0.40000000000000002 height=5.0800000000000001 connect=north]
  led- = Pad [width=0.40000000000000002 height=5.0800000000000001 connect=south]
  nc = Pad [width=0.40000000000000002 height=5.0800000000000001 connect=north]  # not connected
  gnd_2 = Pad [width=0.40000000000000002 height=5.0800000000000001 connect=south]
  rst = Pad [width=0.40000000000000002 height=5.0800000000000001 connect=north]
  dc = Pad [width=0.40000000000000002 height=5.0800000000000001 connect=south]
  mosi = Pad [width=0.40000000000000002 height=5.0800000000000001 connect=south]
  sck = Pad [width=0.40000000000000002 height=5.0800000000000001 connect=south]
  iovdd = Pad [width=0.40000000000000002 height=5.0800000000000001 connect=south]
  vdd = Pad [width=0.40000000000000002 height=5.0800000000000001 connect=south]
  cs = Pad [width=0.40000000000000002 height=5.0800000000000001 connect=north]
  gnd_3 = Pad [width=0.40000000000000002 height=5.0800000000000001 connect=south]
  R3 = Resistor [tolerance=±5% resistance=220 package="1206 [SMD]"]
  R4 = Resistor [tolerance=±5% resistance=220 package="1206 [SMD]"]
  R5 = Resistor [tolerance=±5% resistance=220 package="1206 [SMD]"]
  R6 = Resistor [tolerance=±5% resistance=220 package="1206 [SMD]"]
  o = Resistor [tolerance=±5% resistance=220 package="1206 [SMD]"]
  x = Resistor [tolerance=±5% resistance=220 package="1206 [SMD]"]
  BAT1 = Battery Holders [package=battcon_20mm_4legs]
  U1 = SWITCH_SPDT [package=kps-1290]
  X1 = USB Connectors [package=usb-microb]
  samd21e1 = TQFP32 [chip_label=IC package=TQFP]
  C1 = Ceramic Capacitor [capacitance=100nF package="0603 [SMD, multilayer]"]
  C2 = Ceramic Capacitor [capacitance=100nF package="0603 [SMD, multilayer]"]
  U5 = Voltage Regulator LDO [package=sot23-5]
  D1 = Rectifier Diode [package="Melf DO-213 AA [SMD]"]
  C3 = Ceramic Capacitor [capacitance=100nF package="0603 [SMD, multilayer]"]

nets:
  GND: gnd.pad, led-.pad, gnd_2.pad, gnd_3.pad, R3.Pin_0, R4.Pin_0, R5.Pin_1, R6.Pin_1, o.Pin_0, x.Pin_1, BAT1.-, X1.GND, samd21e1.GND, C1.0, C2.1, U5.GND, C3.1
  N1: led+.pad, iovdd.pad, vdd.pad, samd21e1.VDDANA, samd21e1.VDDIN, U5.OUT, C3.0
  N2: rst.pad, samd21e1.!RESET
  N3: dc.pad, samd21e1.PA05
  N4: mosi.pad, samd21e1.PA06
  N5: sck.pad, samd21e1.PA07
  N6: cs.pad, samd21e1.PA08
  N7: R3.Pin_1, samd21e1.PA16
  N8: R4.Pin_1, samd21e1.PA18
  N9: R5.Pin_0, samd21e1.PA15
  N10: R6.Pin_0, samd21e1.PA22
  N11: o.Pin_1, samd21e1.PA04
  N12: x.Pin_0, samd21e1.PA03
  N13: BAT1.+, D1.anode
  N14: U1.O, D1.cathode
  N15: U1.P, U1.S, X1.VBUS, C2.0, U5.IN, U5.EN
  N16: X1.D+, samd21e1.PA25
  N17: X1.D-, samd21e1.PA24
  N18: samd21e1.VDDCORE, C1.1
